# Fritzing sketch irlock (saved by Fritzing 0.9.0b)
breadboards: 1

parts:
  Part1 = Arduino Uno (Rev3)
  LCD1 = LCD screen
  R1 = Trimmer Potentiometer [maximum_resistance=10kΩ package=THT]
  R2 = Resistor [tolerance=±5% resistance=220 package=THT]
  J1 = Basic Servo
  IC1 = Hex Inverter Schmitt Trigger SN74HC14 [package="DIP (Dual Inline)"]
  IR1 = TSOP312.., 314.. [package=THT]
  D1 = LTE-302 [package=lte-302]
  R3 = Resistor [tolerance=±5% resistance=220 package=THT]
  Lock/Unlock = Pushbutton [package="[THT]"]
  Calibrate_Smartphone = Pushbutton [package="[THT]"]
  Prgm = Pushbutton [package="[THT]"]
  R5 = Resistor [package="2512 [SMD]"]
  R6 = Resistor [package="2512 [SMD]"]
  R4 = Resistor [package="2512 [SMD]"]
  C1 = Ceramic Capacitor [capacitance=100nF package="100 mil [THT, multilayer]"]
  C2 = Ceramic Capacitor [capacitance=100nF package="100 mil [THT, multilayer]"]
  C3 = Ceramic Capacitor [capacitance=100nF package="100 mil [THT, multilayer]"]

nets:
  N1: Part1.D8, LCD1.RS
  N2: Part1.D9_PWM, LCD1.E
  N3: Part1.D10_PWM/SS, LCD1.DB4
  N4: Part1.D11_PWM/MOSI, LCD1.DB5
  N5: Part1.D12/MISO, LCD1.DB6
  N6: Part1.D13/SCK, LCD1.DB7
  N7: Part1.D2, IC1.1Y
  N8: Part1.D3_PWM, R3.Pin_1
  N9: Part1.D4, IR1.Data
  N10: Part1.D6_PWM, IC1.2Y
  N11: Part1.D7, IC1.3Y
  VCC: Part1.5V, LCD1.VDD, R1.leg2, R2.Pin_0, J1.vcc, IC1.VCC, IR1.Vs, R5.Pin_1, R6.Pin_1, R4.Pin_1
  GND: Part1.GND, LCD1.VSS, LCD1.R/W, LCD1.LED-, R1.leg1, J1.gnd, IC1.GND, IR1.GND, D1.C, Lock/Unlock.Pin_3, Lock/Unlock.Pin_4, Calibrate_Smartphone.Pin_3, Calibrate_Smartphone.Pin_4, Prgm.Pin_3, Prgm.Pin_4, C1.0, C2.0, C3.0
  N12: LCD1.V0, R1.wiper
  N13: LCD1.LED+, R2.Pin_1
  N14: IC1.1A, Lock/Unlock.Pin_1, Lock/Unlock.Pin_2, R6.Pin_0, C3.1
  N15: IC1.2A, Calibrate_Smartphone.Pin_1, Calibrate_Smartphone.Pin_2, R5.Pin_0, C2.1
  N16: IC1.3A, Prgm.Pin_1, Prgm.Pin_2, R4.Pin_0, C1.1
  N17: D1.A, R3.Pin_0
